# Fritzing sketch 2X AR EG_V4 (saved by Fritzing 0.9.3b)
circuit board: 4cm x 10.9cm
breadboards: 1

parts:
  Attack = Rotary Potentiometer (Small) [maximum_resistance=1MΩ package=THT]
  power = Header 5x2 [package=avr_icsp]
  1k = Resistor [tolerance=±5% resistance=1k package=THT]
  D1 = Diode [package=diode-1n4148]
  1k_2 = Resistor [tolerance=±5% resistance=1k package=THT]
  ENV_OUT = 3.5mm Switch Jack [part_number=PJ301M-12]
  LED = LED - 3mm [color="Red (633nm)" package="3 mm [THT]"]
  Release = Rotary Potentiometer (Small) [maximum_resistance=1MΩ package=THT]
  1uF = Capacitor [package=cap-pth-small2]
  100k = Resistor [tolerance=±5% resistance=100k package=THT]
  D2 = Diode [package=diode-1n4148]
  100k_2 = Resistor [tolerance=±5% resistance=100k package=THT]
  IN = 3.5mm Switch Jack [part_number=PJ301M-12]
  47k = Resistor [tolerance=±5% resistance=47k package=THT]
  10k = Resistor [tolerance=±5% resistance=10k package=THT]
  D3 = Diode [package=diode-1n4148]
  D4 = Diode [package=diode-1n4148]
  TL072 = TL072 [package="DIP (Dual Inline) [THT]"]
  Composant1 = TL072 [package="DIP (Dual Inline) [THT]"]
  TL072_1 = TL072 [package="DIP (Dual Inline) [THT]"]
  TL072_2 = TL072 [package="DIP (Dual Inline) [THT]"]
  TL072_2_2 = TL072 [package="DIP (Dual Inline) [THT]"]  # not connected
  TL072_1_2 = TL072 [package="DIP (Dual Inline) [THT]"]  # not connected
  part = TL072 [package="DIP (Dual Inline) [THT]"]  # not connected
  TL072_2 = TL072 [package="DIP (Dual Inline) [THT]"]
  IN_2 = 3.5mm Switch Jack [part_number=PJ301M-12]
  ENV_OUT_2 = 3.5mm Switch Jack [part_number=PJ301M-12]
  LED1 = LED - 3mm [color="Red (633nm)" package="3 mm [THT]"]
  1uF_2 = Capacitor [package=cap-pth-small2]
  1k_3 = Resistor [tolerance=±5% resistance=1k package=THT]
  10k_2 = Resistor [tolerance=±5% resistance=10k package=THT]
  47k_2 = Resistor [tolerance=±5% resistance=47k package=THT]
  100k_3 = Resistor [tolerance=±5% resistance=100k package=THT]
  100k_4 = Resistor [tolerance=±5% resistance=100k package=THT]
  1k_4 = Resistor [tolerance=±5% resistance=1k package=THT]
  D5 = Diode [package=diode-1n4148]
  D6 = Diode [package=diode-1n4148]
  D7 = Diode [package=diode-1n4148]
  D8 = Diode [package=diode-1n4148]
  Release_2 = Rotary Potentiometer (Small) [maximum_resistance=1MΩ package=THT]
  Attack_2 = Rotary Potentiometer (Small) [maximum_resistance=1MΩ package=THT]

nets:
  N1: Attack.leg1, D4.C
  N2: Attack.wiper, Attack.leg2, Release.wiper, Release.leg2, 1uF.2, TL072.connector4, TL072_2.pin5
  N3: power.1, power.2, 47k.Pin_0, TL072.connector7, Composant1.pin8, TL072_2.connector7, 47k_2.Pin_0
  N4: power.3, power.4, power.5, power.6, power.7, power.8, ENV_OUT.Pin_1, LED.cathode, 1uF.1, 100k.Pin_0, IN.Pin_1, 10k.Pin_0, IN_2.Pin_1, ENV_OUT_2.Pin_1, LED1.cathode, 1uF_2.1, 10k_2.Pin_0, 100k_4.Pin_0
  N5: power.9, power.10, TL072.connector3, Composant1.pin4, TL072_2.connector3
  N6: 1k.Pin_0, D1.C
  N7: 1k.Pin_1, 1k_2.Pin_0, ENV_OUT.Pin_3
  N8: D1.A, TL072.connector5, TL072.connector6, TL072_2.pin6, TL072_2.pin7
  N9: 1k_2.Pin_1, LED.anode
  N10: Release.leg1, D3.A
  N11: 100k.Pin_1, D2.C, TL072.connector2, TL072_1.pin3
  N12: D2.A, 100k_2.Pin_1
  N13: 100k_2.Pin_0, IN.Pin_3
  N14: 47k.Pin_1, 10k.Pin_1, TL072.connector1, TL072_1.pin2
  N15: D3.C, D4.A, TL072.connector0, TL072_1.pin1
  N16: TL072_2.connector0, D5.A, D6.C
  N17: TL072_2.connector1, 10k_2.Pin_1, 47k_2.Pin_1
  N18: TL072_2.connector2, 100k_4.Pin_1, D7.C
  N19: TL072_2.connector4, 1uF_2.2, Release_2.wiper, Release_2.leg2, Attack_2.wiper, Attack_2.leg2
  N20: TL072_2.connector5, TL072_2.connector6, D8.A
  N21: IN_2.Pin_3, 100k_3.Pin_0
  N22: ENV_OUT_2.Pin_3, 1k_3.Pin_0, 1k_4.Pin_1
  N23: LED1.anode, 1k_3.Pin_1
  N24: 100k_3.Pin_1, D7.A
  N25: 1k_4.Pin_0, D8.C
  N26: D5.C, Attack_2.leg1
  N27: D6.A, Release_2.leg1

notes:
  Léo BARBET
  05/2019
  ______
  2X AR EG V1
  LMNC
  _____________________

custom parts:
  3.5mm Switch Jack: Thonkiconn 3.5mm switching Jack
  TL072: Dual Operational Amplifier
  TL072: Dual Operational Amplifier
  TL072: Dual Operational Amplifier
  TL072: Dual Operational Amplifier
